# Fritzing sketch DigitalThermometer1 (saved by Fritzing 0.9.5d)
breadboards: 1

parts:
  Part1 = Arduino Uno (Rev3)
  DHT11_2 = DHT11 module

nets:
  N1: Part1.D2, DHT11_2.DATA
  5V: Part1.5V, DHT11_2.VCC
  GND: Part1.GND, DHT11_2.GND

custom parts:
  DHT11 module: DHT11 black pcb module
