# Fritzing sketch DigitalThermometer3 (saved by Fritzing 0.9.5d)
breadboards: 1

parts:
  Part1 = Arduino Uno (Rev3)
  DHT11_2 = DHT11 module
  R1 = Trimmer Potentiometer [maximum_resistance=10kΩ package=THT]
  LCD1 = LCD screen

nets:
  N1: Part1.D10_PWM/SS, LCD1.DB4
  N2: Part1.D11_PWM/MOSI, LCD1.DB5
  N3: Part1.D12/MISO, LCD1.DB6
  N4: Part1.D13/SCK, LCD1.DB7
  N5: Part1.D2, DHT11_2.DATA
  N6: Part1.D4, LCD1.RS
  N7: Part1.D6_PWM, LCD1.E
  5V: Part1.5V, DHT11_2.VCC, LCD1.VDD, LCD1.LED+
  GND: Part1.GND, DHT11_2.GND, R1.wiper, R1.leg2, LCD1.VSS, LCD1.R/W, LCD1.LED-
  N8: R1.leg1, LCD1.V0

custom parts:
  DHT11 module: DHT11 black pcb module
