# Fritzing sketch LCD (saved by Fritzing 0.9.5d)
breadboards: 1

parts:
  Part1 = Arduino Uno (Rev3)
  U2 = LCD-16X2 [package=lcd-16x2]
  R1 = Trimmer Potentiometer [maximum_resistance=10kΩ package=THT]

nets:
  N1: Part1.D10_PWM/SS, U2.DB4
  N2: Part1.D11_PWM/MOSI, U2.DB5
  N3: Part1.D12/MISO, U2.DB6
  N4: Part1.D13/SCK, U2.DB7
  N5: Part1.D4, U2.RS
  N6: Part1.D6_PWM, U2.E
  5V: Part1.5V, U2.VDD, U2.A
  GND: Part1.GND, U2.VSS, U2.R_W, U2.K, R1.wiper, R1.leg2
  N7: U2.VO, R1.leg1
